# Fritzing sketch stm32f405_feather_breadboard_FlexSensor (saved by Fritzing 0.9.3b)
breadboards: 1

parts:
  pyboard1 = Micro Python pyboard [part_number=PYBv10b]
  R2 = Basic Flex Resistor
  R3 = Resistor [tolerance=±5% resistance=10k package=THT]

nets:
  N1: pyboard1.X22, R2.Pin_2, R3.Pin_1
  N2: pyboard1.X23_A3V3, R3.Pin_0
  N3: pyboard1.X24_AGND, R2.pin_1
