# Fritzing sketch stm32f405_feather_breadboard_servomotor (saved by Fritzing 0.9.3b)
breadboards: 1

parts:
  pyboard1 = Micro Python pyboard [part_number=PYBv10b]
  J1 = Basic Servo

nets:
  N1: pyboard1.P9A_GND, J1.gnd
  N2: pyboard1.P10A_VIN, J1.vcc
  N3: pyboard1.X1, J1.pulse
