# Fritzing sketch placeboMachine_fall2017 (saved by Fritzing 0.9.3b)
breadboards: 1

parts:
  J2 = Basic Servo
  pyboard2 = Micro Python pyboard [part_number=PYBv10b]
  J3 = Basic Servo
  S2 = Pushbutton [package="[THT]"]

nets:
  GND: J2.gnd, pyboard2.P9A_GND, J3.gnd
  VCC: J2.vcc, pyboard2.P10A_VIN, J3.vcc
  N1: J2.pulse, pyboard2.X3, pyboard2.X7, S2.Pin_1, S2.Pin_2
  N2: pyboard2.X4, J3.pulse
  N3: pyboard2.Y15_3V3, S2.Pin_3, S2.Pin_4
