# Fritzing sketch pyboard_breadboard_buzzer (saved by Fritzing 0.9.3b)
breadboards: 1

parts:
  pyboard1 = Micro Python pyboard [part_number=PYBv10b]
  J1 = Piezo Speaker

nets:
  N1: pyboard1.Y6, J1.pin2
  N2: pyboard1.Y14_GND, J1.pin1
