# Fritzing sketch pyboard_breadboard_motorShield_linearActuator (saved by Fritzing 0.9.3b)

parts:
  pyboard1 = Micro Python pyboard [part_number=PYBv10b]
  Part1 = Adafruit Motor/Stepper/Servo Shield [part_number="Adafruit #1438"]
  JACK1 = 2.1mm Barrel Jack with Terminal Block

nets:
  N1: pyboard1.Y9, Part1.AD5/SCL
  N2: pyboard1.Y10, Part1.AD4/SDA
  N3: pyboard1.Y14_GND, Part1.GND, JACK1.NEG
  N4: pyboard1.Y16_VIN, Part1.+5V
  N5: Part1.VMOTOR, JACK1.POS

custom parts:
  Adafruit Motor/Stepper/Servo Shield: The original Adafruit Motorshield kit is one of our most beloved kits, which is why we decided to make something even better. We have upgraded the shield kit to make the bestest, easiest way to drive DC and Stepper motors. This shield will make quick work of your next robotics project! We kept the ability to drive up to 4 DC motors or 2 stepper motors, but added many improvements: Instead of a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
