# Fritzing sketch pyboard_breadboard_softPotentiometer (saved by Fritzing 0.9.3b)
breadboards: 1

parts:
  pyboard1 = Micro Python pyboard [part_number=PYBv10b]
  R3 = Resistor [tolerance=±5% resistance=10k package=THT]
  SparkFun1 = SoftPot Membrane Potentiometer - 50mm [part_number=SEN-08680]

nets:
  N1: pyboard1.X19, R3.Pin_0, SparkFun1.wiper
  N2: pyboard1.X23_A3V3, SparkFun1.leg1
  N3: pyboard1.X24_AGND, R3.Pin_1, SparkFun1.leg2

custom parts:
  SoftPot Membrane Potentiometer - 50mm: These are very thin variable potentiometers. By pressing down on various parts of the strip, the resistance linearly changes from 100Ohms to 10,000Ohms allowing the user to very accurately calculate the relative position on the strip. Can be used as an accurate positional indicator for CNC head positioning, variable user input (volume level input for example), straight user input (multiple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
