# Fritzing sketch pyboard_breadboard_DRV8871_DCmotor (saved by Fritzing 0.9.3b)
breadboards: 1

parts:
  pyboard1 = Micro Python pyboard [part_number=PYBv10b]
  M1 = DC Motor
  JACK2 = 2.1mm Barrel Jack with Terminal Block
  Part1 = Adafruit DRV8871 [part_number="Adafruit #3190"]

nets:
  N1: pyboard1.X9, Part1.IN1
  N2: pyboard1.X10, Part1.IN2
  N3: pyboard1.X14_GND, JACK2.NEG, Part1.GND
  N4: M1.pin_1, Part1.OUT2
  N5: M1.pin_2, Part1.OUT1
  N6: JACK2.POS, Part1.VMOTOR

custom parts:
  Adafruit DRV8871: Crank up your robotics with powerful Adafruit DRV8871 motor driver breakout board. This motor driver has a lot of great specs that make it useful for a wide variety of mechatronics. In particular, the simple resistor-set current limiting and auto-magic PWM support make it super easy to use. Check out the specs for the DRV8871: 6.5V to 45V motor power voltage Up to 5.5V logic level on IN pins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
