# Fritzing sketch pyboard_breadboard_FSR (saved by Fritzing 0.9.3b)
breadboards: 1

parts:
  pyboard1 = Micro Python pyboard [part_number=PYBv10b]
  R3 = Resistor [tolerance=±5% resistance=10k package=THT]
  J1 = Basic Force Sensing Resistor (FSR) [package=THT]

nets:
  N1: pyboard1.X23_A3V3, J1.pin_1
  N2: pyboard1.X24_AGND, R3.Pin_0
  N3: pyboard1.Y12, R3.Pin_1, J1.pin_0
