# Fritzing sketch pyboard_breadboard_IRsensor (saved by Fritzing 0.9.3b)
breadboards: 1

parts:
  pyboard1 = Micro Python pyboard [part_number=PYBv10b]
  J1 = Infrared Proximity Sensor

nets:
  N1: pyboard1.X20, J1.Vout
  N2: pyboard1.X23_A3V3, J1.Vcc
  N3: pyboard1.X24_AGND, J1.GND
