# Fritzing sketch pyboard_breadboard_IRsensor_and_pushButton (saved by Fritzing 0.9.3b)
breadboards: 1

parts:
  pyboard1 = Micro Python pyboard [part_number=PYBv10b]
  J1 = Infrared Proximity Sensor
  S2 = Pushbutton [package="[THT]"]

nets:
  N1: pyboard1.X6, S2.Pin_3, S2.Pin_4
  N2: pyboard1.X20, J1.Vout
  N3: pyboard1.X23_A3V3, J1.Vcc
  N4: pyboard1.X24_AGND, J1.GND
  N5: pyboard1.Y15_3V3, S2.Pin_1, S2.Pin_2
