# Fritzing sketch pyboard_breadboard_LED (saved by Fritzing 0.9.3b)
breadboards: 1

parts:
  pyboard1 = Micro Python pyboard [part_number=PYBv10b]
  R1 = Resistor [tolerance=±5% resistance=10k package=THT]
  LED1 = LED - 5mm [color="Red (633nm)" package="5 mm [THT]"]

nets:
  N1: pyboard1.X7, LED1.anode
  N2: pyboard1.Y14_GND, R1.Pin_0
  N3: R1.Pin_1, LED1.cathode
