# Fritzing sketch pyboard_breadboard_TB6612Adafruit_TwoDCmotors (saved by Fritzing 0.9.3b)
breadboards: 1

parts:
  pyboard1 = Micro Python pyboard [part_number=PYBv10b]
  R1 = Resistor [tolerance=±5% resistance=10k package=THT]
  Part1 = Adafruit TB6612 DC and Stepper Motor Driver [part_number="Adafruit #2448"]
  M1 = DC Motor
  JACK2 = 2.1mm Barrel Jack with Terminal Block
  M2 = DC Motor

nets:
  N1: pyboard1.X6, Part1.PWMA
  N2: pyboard1.X7, Part1.AIN2
  N3: pyboard1.X8, Part1.AIN1
  N4: pyboard1.Y4, Part1.PWMB
  N5: pyboard1.Y5, Part1.BIN2
  N6: pyboard1.Y6, Part1.BIN1
  N7: pyboard1.Y14_GND, Part1.GND, JACK2.NEG
  N8: pyboard1.Y15_3V3, R1.Pin_1, Part1.VCC
  N9: R1.Pin_0, Part1.STBY
  N10: Part1.Vmotor, Part1.PWRIN, JACK2.POS
  N11: Part1.MOTORA1, M1.pin_2
  N12: Part1.MOTORA2, M1.pin_1
  N13: Part1.MOTORB2, M2.pin_2
  N14: Part1.MOTORB1, M2.pin_1

custom parts:
  Adafruit TB6612 DC and Stepper Motor Driver: Spin two DC motors, step one bi-polar or uni-polar stepper, or fire off two solenoids with 1.2A per channel using the TB6612. These are perhaps better known as "the drivers in our assembled Adafruit Motorshield or Motor HAT." We really like these dual H-bridges, so if you want to control motors without a shield or HAT these are easy to include on any solderless breadboard or perma-proto.
