# Fritzing sketch pyboard_breadboard_TB6612SparkFun_DCmotor (saved by Fritzing 0.9.3b)
breadboards: 1

parts:
  pyboard1 = Micro Python pyboard [part_number=PYBv10b]
  R1 = Resistor [tolerance=±5% resistance=10k package=THT]
  M1 = DC Motor  # not connected
  JACK2 = 2.1mm Barrel Jack with Terminal Block  # not connected
  Part1 = Motor Driver 1A Dual TB6612FNG  # not connected

nets:
  N1: pyboard1.Y15_3V3, R1.Pin_1
