# Fritzing sketch pyboard_breadboard_WS2812LEDs (saved by Fritzing 0.9.3b)

parts:
  pyboard1 = Micro Python pyboard [part_number=PYBv10b]
  JACK1 = 2.1mm Barrel Jack with Terminal Block
  NEOPIXEL1 = Neopixel Strip -- White (60/m) [part_number=1138]

nets:
  N1: pyboard1.X8, NEOPIXEL1.DI
  N2: pyboard1.Y14_GND, JACK1.NEG, NEOPIXEL1.GND
  N3: JACK1.POS, NEOPIXEL1.+5V

custom parts:
  Neopixel Strip -- White (60/m): Neopixel Strip, White, 60 pixels per meter.
