# Fritzing sketch pyboard_breadboard_digtalOut_solenoid (saved by Fritzing 0.9.3b)
breadboards: 1

parts:
  L1 = Solenoid
  D1 = Rectifier Diode [part_number=1N4001 package="300 mil [THT]"]
  pyboard1 = Micro Python pyboard [part_number=PYBv10b]
  Q1 = MOSFET-NCHANNEL [package=to220v]

nets:
  N1: L1.pin1, D1.anode, Q1.D
  N2: L1.pin2, D1.cathode
  N3: pyboard1.P9A_GND, Q1.S
  N4: pyboard1.X3, Q1.G
