# Fritzing sketch pyboard_breadboard_potAndServo (saved by Fritzing 0.9.3b)
breadboards: 1

parts:
  pyboard1 = Micro Python pyboard [part_number=PYBv10b]
  R1 = Rotary Potentiometer (Small) [maximum_resistance=100kΩ package=THT]
  J1 = Basic Servo

nets:
  N1: pyboard1.P9A_GND, J1.gnd
  N2: pyboard1.P10A_VIN, J1.vcc
  N3: pyboard1.X1, J1.pulse
  N4: pyboard1.X23_A3V3, R1.leg2
  N5: pyboard1.X24_AGND, R1.leg1
  N6: pyboard1.Y11, R1.wiper
