# Fritzing sketch pyboard_breadboard_potentiometer (saved by Fritzing 0.9.3b)
breadboards: 1

parts:
  pyboard1 = Micro Python pyboard [part_number=PYBv10b]
  R1 = Rotary Potentiometer (Small) [maximum_resistance=100kΩ package=THT]

nets:
  N1: pyboard1.X22, R1.wiper
  N2: pyboard1.X23_A3V3, R1.leg2
  N3: pyboard1.X24_AGND, R1.leg1
