# Fritzing sketch pyboard_breadboard_servomotor_and_pushButton (saved by Fritzing 0.9.3b)
breadboards: 1

parts:
  pyboard1 = Micro Python pyboard [part_number=PYBv10b]
  J1 = Basic Servo
  S2 = Pushbutton [package="[THT]"]

nets:
  N1: pyboard1.P9A_GND, J1.gnd
  N2: pyboard1.P10A_VIN, J1.vcc
  N3: pyboard1.X1, J1.pulse
  N4: pyboard1.X4, S2.Pin_3, S2.Pin_4
  N5: pyboard1.Y15_3V3, S2.Pin_1, S2.Pin_2
