# Fritzing sketch pyboard_breadboard_servomotor_withPotentiometer (saved by Fritzing 0.9.3b)
breadboards: 1

parts:
  pyboard1 = Micro Python pyboard [part_number=PYBv10b]
  J1 = Basic Servo
  R2 = Rotary Potentiometer (Small) [maximum_resistance=100kΩ package=THT]

nets:
  N1: pyboard1.P9A_GND, J1.gnd
  N2: pyboard1.P10A_VIN, J1.vcc
  N3: pyboard1.X1, J1.pulse
  N4: pyboard1.X22, R2.wiper
  N5: pyboard1.X23_A3V3, R2.leg2
  N6: pyboard1.X24_AGND, R2.leg1
