# Fritzing sketch pyboard_breadboard_startCables (saved by Fritzing 0.9.3b)
breadboards: 1

parts:
  pyboard1 = Micro Python pyboard [part_number=PYBv10b]
  S1 = Pushbutton [package="[THT]"]

nets:
  N1: pyboard1.X4, S1.Pin_1, S1.Pin_2
  N2: pyboard1.Y15_3V3, S1.Pin_3, S1.Pin_4
