# Fritzing sketch pyboard_breadboard_transistor_LED (saved by Fritzing 0.9.3b)
breadboards: 1

parts:
  pyboard1 = Micro Python pyboard [part_number=PYBv10b]
  R1 = Resistor [tolerance=±5% resistance=330 package=THT]
  LED1 = LED - 5mm [color="Red (633nm)" package="5 mm [THT]"]
  Q1 = NPN-Transistor [package="TO92 [THT]"]

nets:
  N1: pyboard1.X7, Q1.B
  N2: pyboard1.Y14_GND, Q1.E
  N3: pyboard1.Y16_VIN, R1.Pin_1
  N4: R1.Pin_0, LED1.anode
  N5: LED1.cathode, Q1.C
